# Fritzing sketch DC Motor Driver (saved by Fritzing 0.9.2b)
breadboards: 1

parts:
  Arduino = Arduino Uno (Rev3) - ICSP
  R1 = Resistor [tolerance=±5% resistance=47 package=THT]
  R2 = Resistor [tolerance=±5% resistance=4.7k package=THT]
  D1_1/4W = Zener Diode [part_number=1N4732A breakdown_voltage=5.6V package="300 mil [THT]"]
  Q1 = Basic FET N-Channel [part_number=IRL2703PBF package="DPak [SMD]"]
  M1 = DC Motor
  D1 = Rectifier Diode [part_number=UF4007 package="300 mil [THT]"]
  R3 = Resistor [tolerance=±5% resistance=47 package=THT]
  C1 = Capacitor [package=cap-pth-small]
  C2 = Capacitor Polarized [part_number="470uF, 10V" package=cpol-radial-10uf-25v]
  C3 = Capacitor [part_number=0.1uF package=cap-pth-small]

nets:
  N1: Arduino.D3_PWM, R1.Pin_0
  GND: R1.Pin_1, R2.Pin_0, R2.Pin_1, D1_1/4W.cathode, D1_1/4W.anode, Q1.Gate, Q1.source, C2.-, C3.2
  N2: Q1.drain, M1.pin_2, D1.anode
  6V: M1.pin_1, R3.Pin_0, C1.1, C2.+, C3.1
  N3: D1.cathode, R3.Pin_1, C1.2

notes:
  Unless otherwise noted,
  all resistors 1/4W
  all capacitors 50V
