# Fritzing sketch Simple DC driver for test (saved by Fritzing 0.9.2b)
breadboards: 1

parts:
  VCC1 = 4 x AAA Battery Mount
  M1 = DC Motor
  R1 = TRIMPOT [package=trimpot_tc33]
  D1 = Diode [package=diode-1n4148]

nets:
  GND: VCC1.-, R1.CCW
  N1: VCC1.+, M1.pin_1
  N2: M1.pin_2, R1.CW, D1.C
