# Fritzing sketch Wireless com test (saved by Fritzing 0.9.2b)
breadboards: 1

parts:
  Arduino = Arduino Uno (Rev3) - ICSP
  Raspberry_Pi1 = Raspberry Pi 2  # not connected
  C1 = Capacitor Polarized [part_number=10uF package=panasonic_h13]
  NRF24L1 = NRF24L01
  NRF24L2 = NRF24L01  # not connected

nets:
  N1: Arduino.ICSP_MISO, Arduino.D12/MISO, NRF24L1.MISO
  N2: Arduino.ICSP_SCK, Arduino.D13/SCK, NRF24L1.SCK
  N3: Arduino.ICSP_MOSI, Arduino.D11_PWM/MOSI, NRF24L1.MOSI
  GND: Arduino.GND, C1.-, NRF24L1.GND
  N4: Arduino.D9_PWM, NRF24L1.CE
  N5: Arduino.D10_PWM/SS, NRF24L1.CSN
  3V3: Arduino.3V3, C1.+, NRF24L1.VCC

custom parts:
  NRF24L01: NRF24L01 module
